# Fritzing sketch ChangingBrightnessDiagram (saved by Fritzing 0.9.2b)
breadboards: 1

parts:
  Part1 = Arduino Uno (Rev3) - ICSP
  LED1 = LED - 3mm [color="Red (633nm)" package="3 mm [THT]"]
  S1 = Pushbutton [package="[THT]"]
  R1 = Resistor [tolerance=±5% resistance=10k package="1206 [SMD]"]
  U1 = POT [package=pot_mammoth]

nets:
  N1: Part1.A5/SCL, U1.A
  N2: Part1.D11_PWM/MOSI, LED1.anode
  N3: Part1.D12/MISO, S1.Pin_1, S1.Pin_2, R1.Pin_1
  N4: Part1.5V, S1.Pin_3, S1.Pin_4, U1.E
  N5: Part1.GND, LED1.cathode, R1.Pin_0, U1.S
