# Fritzing sketch LCD_ABCDiagram (saved by Fritzing 0.9.2b)
breadboards: 1

parts:
  Part1 = Arduino Uno (Rev3)
  U1 = POT [package=pot_mammoth]
  U2 = LCD-16X2 [package=lcd-16x2]
  R1 = Resistor [tolerance=±5% resistance=220 package="1206 [SMD]"]

nets:
  N1: Part1.D11_PWM/MOSI, U2.E
  N2: Part1.D12/MISO, U2.RS
  GND: Part1.GND, U1.S, U2.VSS, U2.R_W, U2.K
  N3: Part1.D4, U2.DB4
  N4: Part1.D5_PWM, U2.DB5
  N5: Part1.D6_PWM, U2.DB6
  N6: Part1.D7, U2.DB7
  5V: Part1.5V, U1.E, U2.VDD, R1.Pin_0
  N7: U1.A, U2.VO
  N8: U2.A, R1.Pin_1
