# Fritzing sketch LCD_MenuSelect (saved by Fritzing 0.9.2b)
breadboards: 1

parts:
  Part1 = Arduino Uno (Rev3)
  U1 = POT [package=pot_mammoth]
  U2 = LCD-16X2 [package=lcd-16x2]
  R1 = Resistor [tolerance=±5% resistance=220 package="1206 [SMD]"]
  S1 = Pushbutton [package="[THT]"]
  R2 = Resistor [tolerance=±5% resistance=10k package="1206 [SMD]"]
  S2 = Pushbutton [package="[THT]"]
  R3 = Resistor [tolerance=±5% resistance=10k package="1206 [SMD]"]

nets:
  N1: Part1.D12/MISO, S1.Pin_1, S1.Pin_2, R2.Pin_1
  N2: Part1.D13/SCK, S2.Pin_1, S2.Pin_2, R3.Pin_1
  GND: Part1.GND, U1.S, U2.VSS, U2.R_W, U2.K, S1.Pin_3, S1.Pin_4, S2.Pin_3, S2.Pin_4
  N3: Part1.D2, U2.E
  N4: Part1.D3_PWM, U2.RS
  N5: Part1.D4, U2.DB4
  N6: Part1.D5_PWM, U2.DB5
  N7: Part1.D6_PWM, U2.DB6
  N8: Part1.D7, U2.DB7
  5V: Part1.5V, U1.E, U2.VDD, R1.Pin_0, R2.Pin_0, R3.Pin_0
  N9: U1.A, U2.VO
  N10: U2.A, R1.Pin_1
