# Fritzing sketch PushAndBlinkDiagram (saved by Fritzing 0.9.2b)
breadboards: 1

parts:
  Part1 = Arduino Uno (Rev3) - ICSP
  LED1 = LED - 3mm [color="Red (633nm)" package="3 mm [THT]"]
  S1 = Pushbutton [package="[THT]"]
  R1 = Resistor [tolerance=±5% resistance=10k package="1206 [SMD]"]

nets:
  N1: Part1.5V, S1.Pin_3, S1.Pin_4
  N2: Part1.D12/MISO, S1.Pin_1, S1.Pin_2, R1.Pin_1
  N3: Part1.D13/SCK, LED1.anode
  N4: Part1.GND, LED1.cathode, R1.Pin_0
