# Fritzing sketch LCD_MenuDiagram (saved by Fritzing 0.9.2b)
breadboards: 1

parts:
  Part1 = Arduino Uno (Rev3)
  U1 = POT [package=pot_mammoth]
  U2 = LCD-16X2 [package=lcd-16x2]
  R1 = Resistor [tolerance=±5% resistance=220 package="1206 [SMD]"]
  S1 = Pushbutton [package="[THT]"]
  R2 = Resistor [tolerance=±5% resistance=10k package="1206 [SMD]"]

nets:
  N1: Part1.D11_PWM/MOSI, U2.RS
  N2: Part1.D12/MISO, U2.E
  N3: Part1.D13/SCK, S1.Pin_1, S1.Pin_2, R2.Pin_1
  GND: Part1.GND, U1.S, U2.VSS, U2.R_W, U2.K, S1.Pin_3, S1.Pin_4, R2.Pin_0
  N4: Part1.D4, U2.DB4
  N5: Part1.D5_PWM, U2.DB5
  N6: Part1.D6_PWM, U2.DB6
  N7: Part1.D7, U2.DB7
  5V: Part1.5V, U1.E, U2.VDD, R1.Pin_0
  N8: U1.A, U2.VO
  N9: U2.A, R1.Pin_1
